# Fritzing sketch garagecore (saved by Fritzing 0.8.7b)
breadboards: 1

parts:
  U1 = Spark Core (v1.0)
  U2 = RELAY [package=relay-g5q]
  U3 = RELAY [package=relay-g5q]
  S1 = Square Pushbutton
  S2 = SPST Switch [package=switch-spdt-smd]

nets:
  N1: U1.A2, U1.3V3
  N2: U1.A3, U1.A6
  N3: U1.A5, U1.VIN
  N4: U1.GND, S2.S
  N5: U1.D0, U2.NC
  N6: U1.D3, U3.NC
  N7: U1.D6, S2.P
  N8: U2.MAIN, U3.MAIN
  N9: U2.NO, S1.leg0
  N10: U3.COIL2, S1.leg1

custom parts:
  Spark Core (v1.0): The Spark Core is a tiny Wi-Fi development board that makes it easy to create internet-connected hardware. The Core is all you need to get started; power it over USB and in minutes you'll be controlling LEDs, switches and motors and collecting data from sensors over the internet! It has 8 digital I/O pins, 8 analog I/O pins, 8 PWM pins; UART (Serial), SPI, I2C, and JTAG peripherals available.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
